# Fritzing sketch CoolingFan+RTC (saved by Fritzing 0.9.2b)
perfboards: 2

parts:
  2SC1816 = NPN-Transistor [package="TO92 [THT]"]
  R2 = Resistor [tolerance=±5% resistance=3k package=THT]
  J1 = female pin header, 20 pins [form="♀ (female)"]
  J2 = female pin header, 20 pins [form="♀ (female)"]
  D2 = Schottky Diode [part_number=ショットキーダイオード package="Melf DO-213 AB [SMD]"]
  パーツ2 = Real Time Clock Module - DS1307 RTC Breakout Board
  ファン1 = DC Motor
  USBシリアル変換(FTDI)1 = FTDI Basic Programmer  # not connected
  J3 = male pin header, 6 pins [form="♂ (male)"]
  Raspberry_Pi2 = Raspberry Pi 2

nets:
  GND: 2SC1816.E, J1.pin3, J1.pin7, J1.pin10, J1.pin15, J1.pin17, J2.pin5, J2.pin13, J2.pin20, パーツ2.GND, J3.pin1, Raspberry_Pi2.GND
  N1: 2SC1816.B, R2.Pin_1
  N2: 2SC1816.C, D2.anode, ファン1.pin_1
  Fan Control: R2.Pin_0, J1.pin20, Raspberry_Pi2.GPIO21
  5V: J1.pin1, J1.pin2, D2.cathode, パーツ2.5V, ファン1.pin_2, Raspberry_Pi2.5V
  Tx: J1.pin4, J3.pin5, Raspberry_Pi2.GPIO14
  Rx: J1.pin5, J3.pin4, Raspberry_Pi2.GPIO15
  N3: J1.pin6, Raspberry_Pi2.GPIO18
  N4: J1.pin8, Raspberry_Pi2.GPIO23
  N5: J1.pin9, Raspberry_Pi2.GPIO24
  N6: J1.pin11, Raspberry_Pi2.GPIO25
  N7: J1.pin12, Raspberry_Pi2.GPIO8
  N8: J1.pin13, Raspberry_Pi2.GPIO7
  N9: J1.pin14, Raspberry_Pi2.ID_SC
  N10: J1.pin16, Raspberry_Pi2.GPIO12
  N11: J1.pin18, Raspberry_Pi2.GPIO16
  N12: J1.pin19, Raspberry_Pi2.GPIO20
  3.3V: J2.pin1, J2.pin9, Raspberry_Pi2.3v3, Raspberry_Pi2.3V3
  SDA: J2.pin2, パーツ2.SDA, Raspberry_Pi2.GPIO2
  SCL: J2.pin3, パーツ2.SCL, Raspberry_Pi2.GPIO3
  N13: J2.pin4, Raspberry_Pi2.GPIO4
  N14: J2.pin6, Raspberry_Pi2.GPIO17
  N15: J2.pin7, Raspberry_Pi2.GPIO27
  N16: J2.pin8, Raspberry_Pi2.GPIO22
  N17: J2.pin10, Raspberry_Pi2.GPIO10
  N18: J2.pin11, Raspberry_Pi2.GPIO9
  N19: J2.pin12, Raspberry_Pi2.GPIO11
  N20: J2.pin14, Raspberry_Pi2.ID_SD
  N21: J2.pin15, Raspberry_Pi2.GPIO5
  N22: J2.pin16, Raspberry_Pi2.GPIO6
  N23: J2.pin17, Raspberry_Pi2.GPIO13
  N24: J2.pin18, Raspberry_Pi2.GPIO19
  N25: J2.pin19, Raspberry_Pi2.GPIO26
