# Fritzing sketch CoolingFan (saved by Fritzing 0.9.2b)
breadboards: 1

parts:
  Raspberry_Pi1 = Raspberry Pi 2
  ファン = DC Motor
  2SC1815 = NPN-Transistor [package="TO92 [THT]"]
  R1 = Resistor [tolerance=±5% resistance=3k package=THT]
  USBシリアル変換(FTDI) = FTDI Basic Programmer
  D1 = Schottky Diode [part_number=ショットキーダイオード package="Melf DO-213 AB [SMD]"]

nets:
  GND: Raspberry_Pi1.GND, 2SC1815.E, USBシリアル変換(FTDI).GND
  N1: Raspberry_Pi1.GPIO21, R1.Pin_0
  N2: Raspberry_Pi1.GPIO15, USBシリアル変換(FTDI).TXO
  N3: Raspberry_Pi1.GPIO14, USBシリアル変換(FTDI).RXI
  N4: Raspberry_Pi1.5V, ファン.pin_1, D1.cathode
  N5: ファン.pin_2, 2SC1815.C, D1.anode
  N6: 2SC1815.B, R1.Pin_1
