# Fritzing sketch コンソールなど用Piシールド(8564) (saved by Fritzing 0.9.3b)
perfboards: 1

parts:
  RTC1 = RTC-8564NB [package="Module(DIP 8P)"]
  パーツ4 = FTDI Basic Programmer
  J2 = male pin header, 2 pins [form="♂ (male)"]
  2SC1816 = NPN-Transistor [package="TO92 [THT]"]
  R2 = Resistor [tolerance=±5% resistance=3k package=THT]
  D2 = Schottky Diode [part_number=1N5817 package="300 mil [THT]"]
  BAT1 = Battery Holders [package=battcon_12mm_pth]
  D3 = Schottky Diode [part_number=1N5817 package="300 mil [THT]"]
  D4 = Schottky Diode [part_number=1N5817 package="300 mil [THT]"]
  J3 = male pin header, 20 pins [form="♂ (male)"]
  J4 = male pin header, 20 pins [form="♂ (male)"]

nets:
  GND: RTC1.GND, パーツ4.GND, 2SC1816.E, BAT1.-, J3.pin3
  N1: RTC1.SDA, J4.pin2
  N2: RTC1.SCL, J4.pin3
  N3: RTC1.VDD, D3.cathode, D4.cathode
  N4: パーツ4.RXI, J3.pin4
  N5: パーツ4.TXO, J3.pin5
  N6: パーツ4.POWER, D4.anode, J4.pin1
  N7: J2.pin1, D2.cathode, J3.pin1
  N8: J2.pin2, 2SC1816.C, D2.anode
  N9: 2SC1816.B, R2.Pin_1
  N10: R2.Pin_0, J3.pin20
  N11: BAT1.+, D3.anode

custom parts:
  RTC-8564NB: Real Time Clock Module and I2C-BUS interface method. This product is a module of the SON 8-pin DIP package. Supply voltage 1.8-5.5V original version by KimuShige
