# Fritzing sketch コンソールなど用Piシールド (saved by Fritzing 0.9.3b)
perfboards: 1

parts:
  パーツ4 = FTDI Basic Programmer
  パーツ5 = Real Time Clock Module - DS1307 RTC Breakout Board
  ファン用端子 = male pin header, 2 pins [form="♂ (male)"]
  2SC1816 = NPN-Transistor [package="TO92 [THT]"]
  R2 = Resistor [tolerance=±5% resistance=3k package=THT]
  D2 = Schottky Diode [part_number=1N5817 package="300 mil [THT]"]
  J3 = double row male pin header, 20 pins [form="♂ (male)"]
  J4 = double row male pin header, 20 pins [form="♂ (male)"]
  J5 = female pin header, 1 pin [form="♀ (female)"]
  J6 = male pin header, 1 pin [form="♂ (male)"]

nets:
  N1: パーツ4.RXI, J4.pin4
  N2: パーツ4.TXO, J4.pin5
  N3: パーツ4.GND, J3.pin13
  N4: パーツ5.5V, J4.pin2
  N5: パーツ5.GND, J3.pin20
  N6: パーツ5.SCL, J3.pin3
  N7: パーツ5.SDA, J3.pin2
  N8: ファン用端子.pin1, D2.cathode, J4.pin1
  N9: ファン用端子.pin2, 2SC1816.C, D2.anode
  N10: 2SC1816.E, J3.pin5
  N11: 2SC1816.B, R2.Pin_1
  N12: R2.Pin_0, J5.pin1
  N13: J4.pin6, J6.pin1

notes:
  シリアルコンソール(/dev/console)
  電池付きRTC
  ファン制御回路
